# Fritzing sketch Accelerometer_DeepSleep (saved by Fritzing 0.9.3b)
breadboards: 1

parts:
  MCU = SparkFun ESP8266 Thing [part_number="ESP8266 Thing"]
  ACCEL = SparkFun IMU Breakout - MPU-9250 [part_number=MPU9250]
  AND_GATE = 74AHC1G08 [package=sot23-5]

nets:
  VCC: MCU.VCC, ACCEL.VDD, AND_GATE.VCC
  N1: MCU.GPIO2, ACCEL.SDA/SDI
  N2: MCU.GPIO14, ACCEL.SCL/SCLK
  N3: MCU.RESET, AND_GATE.Y
  GND: MCU.GND, ACCEL.GND, ACCEL.AD0/SDO, AND_GATE.GND
  N4: MCU.GPIO4, ACCEL.INT, AND_GATE.B
  N5: MCU.GPIO16, AND_GATE.A
