# Fritzing sketch SensorTemperatura (saved by Fritzing 0.9.3b)
breadboards: 1

parts:
  SparkFun = SparkFun ESP8266 Thing
  Componente2 = Adafruit ADS1115 16Bit I2C ADC [part_number="Adafruit #1085"]
  R3 = Temperature Sensor (Thermistor) [thermistor_type=NTC package=THT]
  R2 = Resistor [tolerance=±5% resistance=2.2k package="2010 [SMD]"]

nets:
  VCC: SparkFun.VCC, Componente2.VDD, R3.pin_0
  N1: SparkFun.GPIO2, Componente2.SDA
  N2: SparkFun.GPIO14, Componente2.SCL
  GND: SparkFun.GND, Componente2.ADDR, Componente2.GND
  N3: Componente2.AIN2, R2.Pin_1
  N4: R3.pin_1, R2.Pin_0

custom parts:
  Adafruit ADS1115 16Bit I2C ADC: For microcontrollers without an analog-to-digital converter or when you want a higher-precision ADC, the ADS1115 provides 16-bit precision at 860 samples/second over I2C. The chip can be configured as 4 single-ended input channels, or two differential channels. As a nice bonus, it even includes a programmable gain amplifier, up to x16, to help boost up smaller single/differential signals to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
